# Fritzing sketch PedFeader (saved by Fritzing 0.9.3b)
breadboards: 1

parts:
  LCD1 = LCD screen
  Parça1 = Arduino Nano (Rev3.0) (ICSP)
  LCM1602_IIC2 = LCM1602 IIC [part_number="LCM1602 IIC" chip_label="LCM1602 IIC" package="DIP (Dual Inline) [THT]"]
  J1 = Basic Servo
  Mod1 = KY-022 Infrared Receiver Module [package="Breakout board"]
  LED1 = LED - 5mm [color="Red (633nm)" package="5 mm [THT]"]
  IC2 = DS1302 [package="DIP8 [THT]"]
  R1 = Resistor [tolerance=±5% resistance=220 package="2010 [SMD]"]

nets:
  VSS: LCD1.VSS, LCM1602_IIC2.VSS
  VDD: LCD1.VDD, LCM1602_IIC2.VDD
  N1: LCD1.V0, LCM1602_IIC2.V0
  N2: LCD1.RS, LCM1602_IIC2.RS
  N3: LCD1.R/W, LCM1602_IIC2.RW
  N4: LCD1.E, LCM1602_IIC2.E
  N5: LCD1.DB0, LCM1602_IIC2.D0
  N6: LCD1.DB1, LCM1602_IIC2.D1
  N7: LCD1.DB2, LCM1602_IIC2.D2
  N8: LCD1.DB3, LCM1602_IIC2.D3
  N9: LCD1.DB4, LCM1602_IIC2.D4
  N10: LCD1.DB5, LCM1602_IIC2.D5
  N11: LCD1.DB6, LCM1602_IIC2.D6
  N12: LCD1.DB7, LCM1602_IIC2.D7
  N13: LCD1.LED+, LCM1602_IIC2.A
  N14: LCD1.LED-, LCM1602_IIC2.K
  GND: Parça1.GND, LCM1602_IIC2.GND, J1.gnd, Mod1.-, LED1.anode
  N15: Parça1.D3, R1.Pin_0
  N16: Parça1.D4, IC2.SCLK_-_SPI_Clock
  N17: Parça1.D5, IC2.I/O_-_SPI_Data_In/Out
  N18: Parça1.D6, IC2.CE_-_Chip_Enable
  N19: Parça1.D9, Mod1.S
  VCC: Parça1.5V, LCM1602_IIC2.VCC, J1.vcc, Mod1.Vin
  N20: Parça1.A5, LCM1602_IIC2.SCL
  N21: Parça1.A4, LCM1602_IIC2.SDA
  N22: LCM1602_IIC2.LED_A, LCM1602_IIC2.LED_B
  N23: LED1.cathode, R1.Pin_1

custom parts:
  LCM1602 IIC: I2C-Module to use a 1602 or 2004 LCD on with the wire.h libory Serial LCD Modul
  KY-022 Infrared Receiver Module: KY-022 IR receiver module, reacts to 38kHz infrared light.
